// Logisim project regfile.circ as structural Verilog: 1 circuit, main circuit main
module main (
  input  [4:0] Read_Register_1__rs1,
  input  [4:0] Read_Register_2__rs2,
  input  [4:0] Write_Register__rd,
  input  [31:0] Write_Data,
  input  Write_Enable,
  input  Clock,
  output [31:0] s0_Value,
  output [31:0] s1_Value,
  output [31:0] t0_Value,
  output [31:0] t1_Value,
  output [31:0] a0_Value,
  output [31:0] ra_Value,
  output [31:0] sp_Value,
  output [31:0] Read_Data_1,
  output [31:0] Read_Data_2
);

  wire and_1_out;

  Multiplexer #(.select(5), .width(32)) multiplexer_1 (
    .in0({32{1'b0}}), .in1(ra_Value), .in2(sp_Value), .in5(t0_Value), .in6(t1_Value), .in8(s0_Value),
    .in9(s1_Value), .in10(a0_Value), .out(Read_Data_1), .sel(Read_Register_1__rs1));  // open: in3, in4, in7, in11, in12, in13, in14, in15, in16, in17, in18, in19, in20, in21, in22, in23, in24, in25, in26, in27, in28, in29, in30, in31, en
  Multiplexer #(.select(5), .width(32)) multiplexer_2 (
    .in0({32{1'b0}}), .in1(ra_Value), .in2(sp_Value), .in5(t0_Value), .in6(t1_Value), .in8(s0_Value),
    .in9(s1_Value), .in10(a0_Value), .out(Read_Data_2), .sel(Read_Register_2__rs2));  // open: in3, in4, in7, in11, in12, in13, in14, in15, in16, in17, in18, in19, in20, in21, in22, in23, in24, in25, in26, in27, in28, in29, in30, in31, en
  and and_1 (and_1_out, Write_Enable, Clock);
  Demultiplexer #(.select(5), .width(32)) demultiplexer_1 (
    .out1(ra_Value), .out2(sp_Value), .out5(t0_Value), .out6(t1_Value), .out8(s0_Value), .out9(s1_Value),
    .out10(a0_Value), .in(Write_Data), .sel(Write_Register__rd), .en(and_1_out));  // open: out0, out3, out4, out7, out11, out12, out13, out14, out15, out16, out17, out18, out19, out20, out21, out22, out23, out24, out25, out26, out27, out28, out29, out30, out31

  // Other names for the same wires on the sheet: a0[31:0] = a0_Value; clk = Clock; ra[31:0] = ra_Value;
  //   read_data1[31:0] = Read_Data_1; read_data2[31:0] = Read_Data_2; read_reg1[4:0] = Read_Register_1__rs1;
  //   read_reg2[4:0] = Read_Register_2__rs2; s0[31:0] = s0_Value; s1[31:0] = s1_Value; sp[31:0] = sp_Value;
  //   t0[31:0] = t0_Value; t1[31:0] = t1_Value; write_en = Write_Enable; write_reg[4:0] = Write_Register__rd

  // Notes on the sheet:
  //   INPUTS to your circuit
  //   These are DEBUG/TEST outputs from your circuit.
  //   DON'T CHANGE THE LOCATIONS OF THE INPUTS AND OUTPUTS!
  //   OUTPUTS from your circuit
endmodule
